// Logisim project Contador_gray_4_bits.circ as structural Verilog: 1 circuit, main circuit main
module main (
);

  wire and_1_out, and_2_out, button_1_out, j_k_ff_1_q, j_k_ff_2_q, j_k_ff_3_q, j_k_ff_4_q, xor_1_out,
       xor_2_out, xor_3_out;

  Button button_1 (.out(button_1_out));
  J_K_Flip_Flop j_k_ff_1 (
    .J(button_1_out), .K(button_1_out), .clk(button_1_out), .Q(j_k_ff_1_q));  // open: Qn, preset, reset
  xor xor_1 (xor_1_out, j_k_ff_1_q, j_k_ff_2_q);
  LED led_1 (.in(xor_1_out));
  J_K_Flip_Flop j_k_ff_2 (
    .J(j_k_ff_1_q), .K(j_k_ff_1_q), .clk(button_1_out), .Q(j_k_ff_2_q));  // open: Qn, preset, reset
  and and_1 (and_1_out, j_k_ff_1_q, j_k_ff_2_q);
  xor xor_2 (xor_2_out, j_k_ff_2_q, j_k_ff_3_q);
  LED led_2 (.in(xor_2_out));
  J_K_Flip_Flop j_k_ff_3 (.J(and_1_out), .K(and_1_out), .clk(button_1_out), .Q(j_k_ff_3_q));  // open: Qn, preset, reset
  and and_2 (and_2_out, and_1_out, j_k_ff_3_q);
  xor xor_3 (xor_3_out, j_k_ff_3_q, j_k_ff_4_q);
  LED led_3 (.in(xor_3_out));
  J_K_Flip_Flop j_k_ff_4 (.J(and_2_out), .K(and_2_out), .clk(button_1_out), .Q(j_k_ff_4_q));  // open: Qn, preset, reset
  LED led_4 (.in(j_k_ff_4_q));
endmodule
