// Logisim project Elevador_vhdl.circ as structural Verilog
module main (
);

  wire button_1_out, button_2_out, elevador_1_descer, elevador_1_subir;
  wire [3:0] dipswitch_1_sw1, elevador_1_sensor_andar;

  DipSwitch dipswitch_1 (
    .sw1(dipswitch_1_sw1[0]), .sw2(dipswitch_1_sw1[0]), .sw3(dipswitch_1_sw1[0]), .sw4(dipswitch_1_sw1[0]));  // open: sw5, sw6, sw7, sw8
  Button button_1 (.out(button_1_out));
  Button button_2 (.out(button_2_out));
  LED led_1 (.in(elevador_1_subir));
  elevador elevador_1 (
    .Clock(button_1_out), .Reset(button_2_out), .Escolha_andar(dipswitch_1_sw1), .Subir(elevador_1_subir),
    .Descer(elevador_1_descer), .Sensor_andar(elevador_1_sensor_andar));
  LED led_2 (.in(elevador_1_descer));
  DotMatrix #(.matrixcols(4), .matrixrows(4)) dotmatrix_1 (
    .col0(elevador_1_sensor_andar), .col1(elevador_1_sensor_andar));  // open: col2, col3
  // Pins of 1 and 4 bits meet at dipswitch_1_sw1
endmodule

// VHDL entity elevador, as the project stores it:
library ieee;
use ieee.std_logic_1164.all;
use ieee.numeric_std.all;

ENTITY elevador IS
    PORT (Clock, Reset : IN STD_LOGIC;
    Escolha_andar : IN STD_LOGIC_VECTOR(3 downto 0);
    Subir, Descer : OUT STD_LOGIC; 
    Sensor_andar: OUT STD_LOGIC_VECTOR(3 downto 0));
END elevador;

ARCHITECTURE Behavior OF elevador IS
    TYPE estado_elevador IS (subindo, descendo, parado);
    SIGNAL estado_atual, proximo_estado : estado_elevador;
    SIGNAL s_sensor_andar: std_logic_vector(3 downto 0);
    
BEGIN
    PROCESS (Reset, Clock)
begin
        if Reset = '1' then
            s_sensor_andar <= "0000";      --terreo
            Estado_atual <= parado;     --parado
        END IF;

        if clock'event and clock = '1' then
	    estado_atual <= proximo_estado;    
        END IF;
    END PROCESS;

    PROCESS (Estado_atual, Proximo_estado, sensor_andar, escolha_andar, subir, descer, s_sensor_andar)
        variable int_sensor : integer;
        variable int_escolha: integer;   
begin
    int_sensor := to_integer((unsigned(s_sensor_andar)));
    int_escolha := to_integer((unsigned(escolha_andar)));

    case Estado_atual is

        when Parado =>   
            if int_sensor = int_escolha then --se estiver no andar certo: parado
                Proximo_estado <= parado;
            else
                if int_sensor < int_escolha then    --se estiver no andar inferior Ã  escolha: subindo
                    Proximo_estado <= subindo;
                else       --se estiver no andar superior Ã  escolha: descendo
                    Proximo_estado <= descendo;   
                END IF;
            END IF;

        when Subindo =>

            if int_sensor = int_escolha then
                Proximo_estado <= parado;       --quando chegar, para o elevador
            END IF;

            if s_sensor_andar = "0000" then
                s_sensor_andar <= "0001";
            elsif s_sensor_andar = "1111" then
                Proximo_estado <= parado;
            else
                s_sensor_andar <= std_logic_vector(unsigned(s_sensor_andar) sll 1);      -- desloca Ã  esquerda

            END IF;
        
        when Descendo =>

            if int_sensor = int_escolha then
                Proximo_estado <= parado;       --quando chegar, para o elevador
            END IF;
 
            s_sensor_andar <= std_logic_vector(unsigned(s_sensor_andar) srl 1);      -- desloca Ã  direita
            
        END CASE;

        END PROCESS;
        sensor_andar <= s_sensor_andar;
        -- atribui saÃ­da
        Subir <= '1' when estado_atual = subindo else '0';
        Descer <=  '1' when estado_atual = descendo else '0';
        
END Behavior;
