// Digital circuit testes.dig as structural Verilog
module testes (
  input  in_2,
  input  in_3,
  input  [3:0] in_4,
  output [3:0] out_1
);

  wire u_elevador_alo;

  elevador #(.applicationType("GHDL")) u_elevador (
    .Clock(in_2), .Reset(in_3), .Escolha_andar(in_4), .Sensor_andar(out_1), .alo(u_elevador_alo));
  LED led_1 (.in(u_elevador_alo));
endmodule

/* Code of elevador:
library ieee;
use ieee.std_logic_1164.all;
use ieee.numeric_std.all;

ENTITY elevador IS
    PORT (Clock, Reset : IN STD_LOGIC;
    Escolha_andar : IN STD_LOGIC_VECTOR(3 downto 0);
    Sensor_andar: OUT STD_LOGIC_VECTOR(3 downto 0);
    alo: out std_logic);
END elevador;

ARCHITECTURE Behavior OF elevador IS
    TYPE estado_elevador IS (parado);
    SIGNAL estado_atual, proximo_estado : estado_elevador;
	signal s_sensor_andar: std_logic_vector(3 downto 0);
    
BEGIN
    PROCESS (Reset, Clock)
begin
        if Reset = '1' then
            Estado_atual <= parado;     --parado
        END IF;

        if clock'event and clock = '1' then
	    estado_atual <= proximo_estado;    
	    
        END IF;
    END PROCESS;

    PROCESS (Estado_atual, Proximo_estado, escolha_andar)
	--variable s_sensor_andar : std_logic_vector(3 downto 0);
	variable int_sensor : integer;
begin

	int_sensor := to_integer(unsigned(escolha_andar));

    case Estado_atual is
	
        when Parado =>   
	    
	sensor_andar <= escolha_andar;
	    if int_sensor = 1 then
		s_sensor_andar <= "0001";	
		alo <= '1';		

	    elsif escolha_andar = "0010" then
		s_sensor_andar <= "0010";
		alo <= '1';
	    
	END IF;

        END CASE;

        END PROCESS;
        
END Behavior;
*/
